# Fritzing sketch Heart LED Circle Start (saved by Fritzing 0.8.7b)
circuit board: 10.9753cm x 9.86798cm
breadboards: 1

parts:
  U3 = attiny85 [package=dip]
  U4 = 74HC595 [package="DIP16 [THT]"]
  LED1 = LED - 5mm [color="Blue (470nm)" package="5 mm [THT]"]
  LED2 = LED - 5mm [color="Blue (470nm)" package="5 mm [THT]"]
  LED3 = LED - 5mm [color="Blue (470nm)" package="5 mm [THT]"]
  LED4 = LED - 5mm [color="Blue (470nm)" package="5 mm [THT]"]
  LED5 = LED - 5mm [color="Blue (470nm)" package="5 mm [THT]"]
  LED6 = LED - 5mm [color="Blue (470nm)" package="5 mm [THT]"]
  LED7 = LED - 5mm [color="Blue (470nm)" package="5 mm [THT]"]
  LED8 = LED - 5mm [color="Blue (470nm)" package="5 mm [THT]"]
  VCC1 = Battery
  C1 = Electrolytic Capacitor [capacitance=1µF package="100 mil [THT, electrolytic]"]
  J5 = female pin header, 1 pin [form="♀ (female)"]  # not connected
  J6 = female pin header, 1 pin [form="♀ (female)"]  # not connected

nets:
  N1: U3.Pin_4, U4.GND, U4.OE, LED1.cathode, LED2.cathode, LED3.cathode, LED4.cathode, LED5.cathode, LED6.cathode, LED7.cathode, LED8.cathode, VCC1.-, C1.-
  N2: U3.Pin_5, U4.DS
  N3: U3.Pin_6, U4.ST_CP
  N4: U3.Pin_7, U4.SH_CP
  N5: U3.Pin_8, U4.MR, U4.VCC, VCC1.+, C1.+
  N6: U4.Q1, LED1.anode
  N7: U4.Q2, LED3.anode
  N8: U4.Q3, LED4.anode
  N9: U4.Q4, LED2.anode
  N10: U4.Q5, LED8.anode
  N11: U4.Q6, LED7.anode
  N12: U4.Q7, LED6.anode
  N13: U4.Q0, LED5.anode
